# Fritzing sketch Fritzing schematic (saved by Fritzing 0.9.3b)

parts:
  U1 = NodeMCU V1.0
  Load_Cell1 = Load Cell - Red/white/black/green
  Adafruit_HX711_ADC_Breakout1 = Adafruit HX711 ADC Breakout [part_number=#5974]
  DHT1 = DHT11 Humitidy and Temperature Sensor
  Part1 = SRF05 Ultrasonic Rangefinder
  U2 = BATTERY-2 [package=battery-aa]
  TP1 = TP4056 [chip_label=TP4056 package="DIP (Dual Inline) [THT]"]
  D1 = SOLAR-IXYS [package=solarbit-12x1]

nets:
  N1: U1.D1, Part1.Trig
  N2: U1.D2, DHT1.DATA
  3V3: U1.3V3, DHT1.VDD
  GND: U1.GND, Load_Cell1.wire3, Adafruit_HX711_ADC_Breakout1.GND, DHT1.GND, Part1.GND, TP1.pin6
  N3: U1.D5, Adafruit_HX711_ADC_Breakout1.DATAOUT
  N4: U1.D6, Adafruit_HX711_ADC_Breakout1.SCLK
  N5: U1.D7, Part1.Echo
  VIN: U1.Vin, Adafruit_HX711_ADC_Breakout1.V+, Part1.VCC, TP1.pin3
  N6: Load_Cell1.wire1, Adafruit_HX711_ADC_Breakout1.VPP
  N7: Load_Cell1.wire2, Adafruit_HX711_ADC_Breakout1.A-
  N8: Load_Cell1.wire4, Adafruit_HX711_ADC_Breakout1.A+
  N9: U2.-1, TP1.pin5
  N10: U2.+1, TP1.pin4
  N11: TP1.pin1, D1.C
  N12: TP1.pin2, D1.A

notes:
  RED (E+)
  BLACK (E-)
  WHITE (A-)
  GREEN (A+)
  HX711

custom parts:
  NodeMCU V1.0: ESP8266 based NodeMCU
  Load Cell - Red/white/black/green: A rectangle load cell/weighting pressure Sensor with four wires - Red, white, black, green. Normally corresponding with E+, E-, A+, A- respectively.
  Adafruit HX711 ADC Breakout: If you are feeling the stress and strain of modern life a Wheatstone bridge and you want to quantify it, this handy breakout will do the job, no sweat! The Adafruit HX711 Breakout contains a super-high-resolution 24-Bit differential ADC with extra gain circuitry that makes it perfect for measuring strain gauges / load cells or other sensors that have four wires that are connected in a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
  DHT11 Humitidy and Temperature Sensor: DHT11 Humidity and Temperature Sensor
  TP4056: A DIP stand-in part for whatever IC you want. With 6 pins on a 300mil dual inline package (DIP) footprint.
